# Fritzing sketch ColorPicker (saved by Fritzing 0.8.3b)
circuit board: 5.13641cm x 3.97933cm
breadboards: 1

parts:
  Part1 = Arduino Micro (Rev3)
  R1 = Resistor [tolerance=±5% resistance=220 package=THT]
  R2 = Resistor [tolerance=±5% resistance=220 package=THT]
  R3 = Resistor [tolerance=±5% resistance=220 package=THT]
  LED1 = RGB LED (com. cathode, rbg) [package="5 mm [THT]"]

nets:
  N1: Part1.GND, LED1.common_cathode
  N2: Part1.D9_PWM/A9, R1.Pin_1
  N3: Part1.D10_PWM/A10, R2.Pin_1
  N4: Part1.D11_PWM, R3.Pin_1
  N5: R1.Pin_0, LED1.green_anode
  N6: R2.Pin_0, LED1.blue_anode
  N7: R3.Pin_0, LED1.red_anode
